# Fritzing sketch kitchen_guard (saved by Fritzing 0.9.3b)
circuit board: 8.46667cm x 5.64444cm
breadboards: 1

parts:
  WeMos_D1_Mini1 = WeMos D1 Mini
  R1 = Resistor [tolerance=±5% resistance=150 package=THT]
  R2 = Resistor [tolerance=±5% resistance=1.5k package=THT]
  R3 = Resistor [tolerance=±5% resistance=3.3k package=THT]
  U1 = GAS_SENSOR [package=mq-3]

nets:
  N1: WeMos_D1_Mini1.A0, R2.Pin_1, R3.Pin_0
  N2: WeMos_D1_Mini1.G, R3.Pin_1, U1.B1
  N3: R1.Pin_1, R2.Pin_0

notes:
  [MQ-2 sensor module]
